// Logisim project ALU.circ as structural Verilog: 3 circuits, main circuit alu
module alu (
  input  [31:0] X,
  input  [31:0] Y,
  input  [3:0] AluOP,
  output Signed_Overflow,
  output UnSigned_Overflow,
  output Equal,
  output [31:0] Result,
  output [31:0] Result_2
);

  wire comparator_1_lt, comparator_2_lt;
  wire [1:0] adderwoverflowdetection_1_cf, subtractorwoverflowdetection_1_cf;
  wire [31:0] adderwoverflowdetection_1_result_of_the_operation_46cd1f9d, and_1_out, bit_extender_1_out,
       bit_extender_2_out, divider_1_out, divider_1_rem, multiplier_1_cout, multiplier_1_out, not_1_out,
       or_1_out, or_2_out, shifter_1_out, shifter_2_out, shifter_3_out,
       subtractorwoverflowdetection_1_result_of_the_operation_46cd1f9d, xor_1_out;

  // Probe on X
  // Probe on X
  // Probe on Y
  // Probe on Y
  Shifter #(.width(32)) shifter_1 (.in(X), .\dist (Y[4:0]), .out(shifter_1_out));
  Shifter #(.shift("ar"), .width(32)) shifter_2 (.in(X), .\dist (Y[4:0]), .out(shifter_2_out));
  Shifter #(.shift("lr"), .width(32)) shifter_3 (.in(X), .\dist (Y[4:0]), .out(shifter_3_out));
  Multiplier #(.width(32)) multiplier_1 (.a(X), .b(Y), .out(multiplier_1_out), .cout(multiplier_1_cout));  // open: cin
  Divider #(.width(32)) divider_1 (.a(X), .b(Y), .out(divider_1_out), .rem(divider_1_rem));  // open: upper
  AdderwOverflowDetection adderwoverflowdetection_1 (
    .X(X), .Y(Y),
    .Result_of_the_operation_46cd1f9d(adderwoverflowdetection_1_result_of_the_operation_46cd1f9d),
    .CF(adderwoverflowdetection_1_cf[0]), .OF(adderwoverflowdetection_1_cf[1]));  // open: in_3
  SubtractorwOverflowDetection subtractorwoverflowdetection_1 (
    .X(X), .Y(Y),
    .Result_of_the_operation_46cd1f9d(subtractorwoverflowdetection_1_result_of_the_operation_46cd1f9d),
    .CF(subtractorwoverflowdetection_1_cf[0]), .OF(subtractorwoverflowdetection_1_cf[1]));  // open: in_3
  assign and_1_out = X & Y;  // AND_Gate and_1, 32 bits wide
  assign or_1_out = X | Y;  // OR_Gate or_1, 32 bits wide
  assign xor_1_out = X ^ Y;  // XOR_Gate xor_1, 32 bits wide
  assign or_2_out = X | Y;  // OR_Gate or_2, 32 bits wide
  Comparator #(.width(32)) comparator_1 (.a(X), .b(Y), .lt(comparator_1_lt));  // open: gt, eq
  Comparator #(.mode("unsigned"), .width(32)) comparator_2 (
    .a(X), .b(Y), .eq(Equal), .lt(comparator_2_lt));  // open: gt
  // Probe on AluOP
  assign not_1_out = ~or_2_out;  // NOT_Gate not_1, 32 bits wide
  // Probe on Result
  // Probe on Result
  Multiplexer #(.enable("true"), .select(4), .width(2)) multiplexer_1 (
    .in0(2'b00), .in1(2'b00), .in2(2'b00), .in3(2'b00), .in4(2'b00), .in5(adderwoverflowdetection_1_cf),
    .in6(subtractorwoverflowdetection_1_cf), .in7(2'b00), .in8(2'b00), .in9(2'b00), .in10(2'b00),
    .in11(2'b00), .in12(2'b00), .in13(2'b00), .in14(2'b00), .in15(2'b00),
    .out({Signed_Overflow, UnSigned_Overflow}), .sel(AluOP));  // open: en
  // Probe on Result_2
  assign bit_extender_1_out = {{31{1'b0}}, comparator_1_lt};  // Bit_Extender bit_extender_1
  assign bit_extender_2_out = {{31{1'b0}}, comparator_2_lt};  // Bit_Extender bit_extender_2
  Multiplexer #(.enable("true"), .select(4), .width(32)) multiplexer_2 (
    .in0({32{1'b0}}), .in1({32{1'b0}}), .in2({32{1'b0}}), .in3(multiplier_1_cout), .in4(divider_1_rem),
    .in5({32{1'b0}}), .in6({32{1'b0}}), .in7({32{1'b0}}), .in8({32{1'b0}}), .in9({32{1'b0}}),
    .in10({32{1'b0}}), .in11({32{1'b0}}), .in12({32{1'b0}}), .in13({32{1'b0}}), .in14({32{1'b0}}),
    .in15({32{1'b0}}), .out(Result_2), .sel(AluOP));  // open: en
  Multiplexer #(.select(4), .width(32)) multiplexer_3 (
    .in0(shifter_1_out), .in1(shifter_2_out), .in2(shifter_3_out), .in3(multiplier_1_out),
    .in4(divider_1_out), .in5(adderwoverflowdetection_1_result_of_the_operation_46cd1f9d),
    .in6(subtractorwoverflowdetection_1_result_of_the_operation_46cd1f9d), .in7(and_1_out), .in8(or_1_out),
    .in9(xor_1_out), .in10(not_1_out), .in11(bit_extender_1_out), .in12(bit_extender_2_out),
    .in13({32{1'b0}}), .in14({32{1'b0}}), .in15({32{1'b0}}), .out(Result), .sel(AluOP));

  // Other names for the same wires on the sheet: CF = UnSigned_Overflow; OF = Signed_Overflow;
  //   Result2[31:0] = Result_2; S[3:0] = AluOP

  // Notes on the sheet:
  //   Input
  //   Output
  //   Debug
endmodule

// +
module AdderwOverflowDetection (
  input  [31:0] X,
  input  [31:0] Y,
  input  in_3,
  output [31:0] Result_of_the_operation_46cd1f9d,
  output CF,
  output OF
);

  wire adder_1_cout;

  // Probe on X
  Adder #(.width(31)) adder_1 (
    .a(X[30:0]), .b(Y[30:0]), .out(Result_of_the_operation_46cd1f9d[30:0]), .cin(in_3), .cout(adder_1_cout));
  Adder #(.width(1)) adder_2 (
    .a(X[31]), .b(Y[31]), .out(Result_of_the_operation_46cd1f9d[31]), .cin(adder_1_cout), .cout(CF));
  // Probe on Y
  xor xor_1 (OF, adder_1_cout, CF);
  // Probe on Result_of_the_operation_46cd1f9d

  // Other names for the same wires on the sheet: cin = in_3; Result[31:0] = Result_of_the_operation_46cd1f9d
endmodule

// -
module SubtractorwOverflowDetection (
  input  [31:0] X,
  input  [31:0] Y,
  input  in_3,
  output [31:0] Result_of_the_operation_46cd1f9d,
  output CF,
  output OF
);

  wire subtractor_1_bout;

  // Probe on X
  Subtractor #(.width(31)) subtractor_1 (
    .a(X[30:0]), .b(Y[30:0]), .out(Result_of_the_operation_46cd1f9d[30:0]), .bin(in_3),
    .bout(subtractor_1_bout));
  Subtractor #(.width(1)) subtractor_2 (
    .a(X[31]), .b(Y[31]), .out(Result_of_the_operation_46cd1f9d[31]), .bin(subtractor_1_bout), .bout(CF));
  // Probe on Y
  xor xor_1 (OF, subtractor_1_bout, CF);
  // Probe on Result_of_the_operation_46cd1f9d

  // Other names for the same wires on the sheet: bin = in_3; Result[31:0] = Result_of_the_operation_46cd1f9d
endmodule
