// Logisim project Control_Unit.circ as structural Verilog: 1 circuit, main circuit control_unit
// RegWrite
module control_unit (
  input  [5:0] op,
  input  [5:0] Funct,
  output isJAL,
  output MemRead,
  output isShamt,
  output MemWrite,
  output MemtoReg,
  output Jump,
  output RegWrite,
  output Branch,
  output BneOrBeq,
  output [3:0] ALUOp,
  output RegDst,
  output ALUSrc,
  output IsJR,
  output IsSyscall,
  output IsCOP0,
  output ZeroExtend,
  output ReadRs,
  output ReadRt
);

  wire funct_decoder_1_isjr, funct_decoder_1_isshamt, funct_decoder_1_issyscall, IsSpecial, not_1_out;
  wire [3:0] alu_decoder_1_aluop0, funct_decoder_1_alu3;

  Opcode_decoder opcode_decoder_1 (
    .op0(op[5]), .op1(op[4]), .op2(op[3]), .op3(op[2]), .op4(op[1]), .op5(op[0]), .MemRead(MemRead),
    .MemWrite(MemWrite), .ALUSrc(ALUSrc), .Jump(Jump), .MemtoReg(MemtoReg), .Branch(Branch), .RegDst(RegDst),
    .RegWrite(RegWrite), .BneBeq(BneOrBeq), .IsJAL(isJAL), .ZeroExtend(ZeroExtend));
  Funct_Decoder funct_decoder_1 (
    .Funct0(Funct[5]), .Funct1(Funct[4]), .Funct2(Funct[3]), .Funct3(Funct[2]), .Funct4(Funct[1]),
    .Funct5(Funct[0]), .ALU0(funct_decoder_1_alu3[3]), .ALU1(funct_decoder_1_alu3[2]),
    .ALU2(funct_decoder_1_alu3[1]), .ALU3(funct_decoder_1_alu3[0]), .IsJR(funct_decoder_1_isjr),
    .IsSyscall(funct_decoder_1_issyscall), .IsShamt(funct_decoder_1_isshamt));
  ALU_Decoder alu_decoder_1 (
    .Op5(op[5]), .Op4(op[4]), .Op3(op[3]), .Op2(op[2]), .Op1(op[1]), .Op0(op[0]),
    .ALUop3(alu_decoder_1_aluop0[3]), .ALUop2(alu_decoder_1_aluop0[2]), .ALUop1(alu_decoder_1_aluop0[1]),
    .ALUop0(alu_decoder_1_aluop0[0]));
  Multiplexer multiplexer_1 (.in0(1'b0), .in1(funct_decoder_1_issyscall), .out(IsSyscall), .sel(IsSpecial));
  Multiplexer multiplexer_2 (.in0(1'b0), .in1(funct_decoder_1_isjr), .out(IsJR), .sel(IsSpecial));
  Multiplexer multiplexer_3 (.in0(1'b0), .in1(funct_decoder_1_isshamt), .out(isShamt), .sel(IsSpecial));
  not not_1 (not_1_out, IsSpecial);
  Multiplexer #(.width(4)) multiplexer_4 (
    .in0(funct_decoder_1_alu3), .in1(alu_decoder_1_aluop0), .out(ALUOp), .sel(not_1_out));
  RegisterRead_Detector registerread_detector_1 (
    .op0(op[0]), .op1(op[1]), .op2(op[2]), .op3(op[3]), .op4(op[4]), .op5(op[5]), .Funct0(Funct[0]),
    .Funct1(Funct[1]), .Funct2(Funct[2]), .Funct3(Funct[3]), .Funct4(Funct[4]), .Funct5(Funct[5]),
    .ReadRs(ReadRs), .ReadRt(ReadRt));
  and and_1 (IsSpecial, ~op[5], ~op[4], ~op[3], ~op[2], ~op[1], ~op[0]);  // AND_Gate
  and and_2 (IsCOP0, ~op[0], op[1], ~op[2], ~op[3], ~op[4], ~op[5]);  // AND_Gate

  // Notes on the sheet:
  //   Input & Output
  //   OP Decoding Area
  //   Exception Handler
endmodule
