// Logisim project Immediate_Extender.circ as structural Verilog: 1 circuit, main circuit Immediate_Extender
module Immediate_Extender (
  input  ZeroExtend,
  input  [15:0] InputT,
  output [31:0] Output
);

  wire [31:0] bit_extender_1_out, bit_extender_2_out;

  assign bit_extender_1_out = {{16{InputT[15]}}, InputT};  // Bit_Extender bit_extender_1
  assign bit_extender_2_out = {{16{1'b0}}, InputT};  // Bit_Extender bit_extender_2
  Multiplexer #(.width(32)) multiplexer_1 (
    .in0(bit_extender_1_out), .in1(bit_extender_2_out), .out(Output), .sel(ZeroExtend));
endmodule
