// Logisim project Single_Cycle_CPU.circ as structural Verilog: 1 circuit, main circuit main
module main (
);

  wire ALUSrc, and_1_out, and_2_out, BneOrBeq, Branch, Clk, clock_1_out, counter_1_carry, Equal, ExpBlock,
       ExpSrc0, ExpSrc1, ExpSrc2, ExRegWrite, Halt, HasExp, instruction_statistics_1_p1,
       instruction_statistics_1_p2, instruction_statistics_1_p3, IsCOP0, isJAL, isJR, IsRet, IsShamt,
       IsSyscall, Jump, MemRead, MemtoReg, MemWrite, multiplexer_4_out, multiplexer_12_out, not_1_out,
       not_2_out, not_3_out, not_4_out, not_5_out, or_1_out, RegDst, RegRs, RegRt, RegWrite, xor_1_out,
       ZeroExtend;
  wire [3:0] adder_1_out_2, ALUOp, syscall_decoder_1_hex_2, syscall_decoder_1_hex_3, syscall_decoder_1_hex_4,
       syscall_decoder_1_hex_5;
  wire [4:0] immediate_extender_1_p4, multiplexer_7_out, multiplexer_8_out, multiplexer_10_out;
  wire [5:0] instruction_statistics_1_p9;
  wire [7:0] counter_2_q, counter_3_q, counter_4_q;
  wire [8:0] demultiplexer_1_out0, demultiplexer_1_out1;
  wire [15:0] syscall_decoder_1_hex;
  wire [25:0] multiplexer_5_out;
  wire [27:0] adder_1_out;
  wire [31:0] adder_2_out, adder_3_out, bit_extender_1_out, cp0_1_dout, cp0_1_pcout, immediate_extender_1_p3,
       multiplexer_1_out, multiplexer_2_out, multiplexer_6_out, multiplexer_9_out, multiplexer_13_out,
       multiplexer_14_out, multiplexer_15_out, multiplexer_16_out, multiplexer_17_out, multiplexer_18_out,
       multiplexer_19_out, ram_1_dout, regfile_1_p4, regfile_1_p5, register_1_q, register_2_q, rom_1_data,
       rom_2_data, shifter_1_out, undriven;

  Multiplexer #(.width(32)) multiplexer_1 (
    .in0(multiplexer_19_out), .in1(cp0_1_pcout), .out(multiplexer_1_out), .sel(and_1_out));
  and and_1 (and_1_out, IsRet, IsCOP0);
  Clock clock_1 (.out(clock_1_out));
  Multiplexer #(.width(32)) multiplexer_2 (
    .in0(32'h800), .in1(multiplexer_1_out), .out(multiplexer_2_out), .sel(not_1_out));
  not not_1 (not_1_out, HasExp);
  Multiplexer multiplexer_3 (.in0(clock_1_out), .in1(1'b0), .out(Clk), .sel(Halt));
  Register #(.width(32)) register_1 (
    .D(multiplexer_2_out), .Q(register_1_q), .clk(multiplexer_4_out));  // open: en, clr
  Multiplexer multiplexer_4 (.in0(Clk), .in1(not_2_out), .out(multiplexer_4_out), .sel(or_1_out));
  or or_1 (or_1_out, HasExp, and_1_out);
  not not_2 (not_2_out, Clk);
  Counter counter_1 (.carry(counter_1_carry), .clk(Clk));  // open: load, D, count, Q, up, clr
  // Probe on counter_1_carry
  // Probe on counter_2_q
  Demultiplexer #(.width(9)) demultiplexer_1 (
    .out0(demultiplexer_1_out0), .out1(demultiplexer_1_out1), .in(register_1_q[10:2]), .sel(register_1_q[11]));
  Counter counter_2 (.count(instruction_statistics_1_p3), .Q(counter_2_q));  // open: load, D, carry, up, clk, clr
  // Probe on counter_3_q
  ROM #(.addrWidth(9), .dataWidth(32)) rom_1 (.addr(demultiplexer_1_out0), .data(rom_1_data));
  Counter counter_3 (.count(instruction_statistics_1_p2), .Q(counter_3_q), .clk(Clk));  // open: load, D, carry, up, clr
  ROM #(.addrWidth(9), .dataWidth(32)) rom_2 (.addr(demultiplexer_1_out1), .data(rom_2_data));
  Counter counter_4 (.count(instruction_statistics_1_p1), .Q(counter_4_q));  // open: load, D, carry, up, clk, clr
  // Probe on counter_4_q
  Adder #(.width(32)) adder_1 (.a(32'h4), .b(register_1_q), .out({adder_1_out_2, adder_1_out}));  // open: cin, cout
  // Instruction_Statistics instruction_statistics_1: pin names not known; wires that end beside it: instruction_statistics_1_p1, instruction_statistics_1_p2, instruction_statistics_1_p3, instruction_statistics_1_p9[5], instruction_statistics_1_p9[4], instruction_statistics_1_p9[3], instruction_statistics_1_p9[2], instruction_statistics_1_p9[1], instruction_statistics_1_p9[0]
  Multiplexer #(.width(32)) multiplexer_5 (
    .in0(rom_1_data), .in1(rom_2_data), .out({instruction_statistics_1_p9, multiplexer_5_out}),
    .sel(register_1_q[11]));
  Adder #(.width(32)) adder_2 (.a(register_1_q), .b(32'h4), .out(adder_2_out));  // open: cin, cout
  Register #(.width(32)) register_2 (.D(register_1_q), .Q(register_2_q), .clk(HasExp));  // open: en, clr
  control_unit control_unit_1 (
    .op(instruction_statistics_1_p9), .Funct(multiplexer_5_out[5:0]), .ALUOp(ALUOp), .isJAL(isJAL),
    .isShamt(IsShamt), .MemtoReg(MemtoReg), .RegWrite(RegWrite), .BneOrBeq(BneOrBeq), .ALUSrc(ALUSrc),
    .IsSyscall(IsSyscall), .ZeroExtend(ZeroExtend), .IsCOP0(IsCOP0), .ReadRs(RegRs), .ReadRt(RegRt),
    .MemRead(MemRead), .Jump(Jump), .Branch(Branch), .MemWrite(MemWrite), .RegDst(RegDst), .IsJR(isJR));
  CP0 cp0_1 (
    .Inst({instruction_statistics_1_p9, multiplexer_5_out}), .Expsrc0(ExpSrc0), .Expsrc1(ExpSrc1),
    .Expsrc2(ExpSrc2), .Din(immediate_extender_1_p3), .PCin(register_2_q), .clk(Clk), .Enable(IsCOP0),
    .PCout(cp0_1_pcout), .Dout(cp0_1_dout), .IsRet(IsRet), .ExRegWrite(ExRegWrite), .HasExp(HasExp),
    .ExpBlock(ExpBlock));
  Multiplexer #(.width(32)) multiplexer_6 (
    .in0(cp0_1_dout), .in1(multiplexer_9_out), .out(multiplexer_6_out), .sel(not_3_out));
  Multiplexer #(.width(5)) multiplexer_7 (
    .in0(multiplexer_5_out[20:16]), .in1(multiplexer_5_out[15:11]), .out(multiplexer_7_out), .sel(RegDst));
  not not_3 (not_3_out, IsCOP0);
  not not_4 (not_4_out, isJAL);
  Multiplexer #(.width(5)) multiplexer_8 (
    .in0(multiplexer_7_out), .in1({5{1'b0}}), .out(multiplexer_8_out), .sel(isJAL));
  Multiplexer #(.width(32)) multiplexer_9 (
    .in0(adder_2_out), .in1(multiplexer_17_out), .out(multiplexer_9_out), .sel(not_4_out));
  Multiplexer #(.width(5)) multiplexer_10 (
    .in0(multiplexer_5_out[20:16]), .out(multiplexer_10_out), .sel(IsSyscall));  // open: in1
  // immediate_extender immediate_extender_1: pin names not known; wires that end beside it: ZeroExtend, multiplexer_5_out[15:0], immediate_extender_1_p3, immediate_extender_1_p4
  Multiplexer #(.width(5)) multiplexer_11 (
    .in0(multiplexer_5_out[25:21]), .in1({5{1'b0}}), .out(immediate_extender_1_p4), .sel(IsSyscall));
  Multiplexer multiplexer_12 (.in0(RegWrite), .in1(ExRegWrite), .out(multiplexer_12_out), .sel(IsCOP0));
  // regfile regfile_1: pin names not known; wires that end beside it: multiplexer_10_out, multiplexer_8_out, multiplexer_6_out, regfile_1_p4, regfile_1_p5
  Multiplexer #(.width(32)) multiplexer_13 (
    .in0(regfile_1_p5), .in1(immediate_extender_1_p3), .out(multiplexer_13_out), .sel(ALUSrc));
  assign bit_extender_1_out = {{27{1'b0}}, multiplexer_5_out[10:6]};  // Bit_Extender bit_extender_1
  Multiplexer #(.width(32)) multiplexer_14 (
    .in0(regfile_1_p4), .in1(immediate_extender_1_p3), .out(multiplexer_14_out), .sel(IsShamt));
  Multiplexer #(.width(32)) multiplexer_15 (
    .in0(multiplexer_13_out), .in1(bit_extender_1_out), .out(multiplexer_15_out), .sel(IsShamt));
  Button button_1 (.out(ExpSrc0));
  syscall_decoder syscall_decoder_1 (
    .clk(Clk), .Enable(IsSyscall), .v0(regfile_1_p4), .a0(immediate_extender_1_p3), .Halt(Halt),
    .Hex({syscall_decoder_1_hex_5, syscall_decoder_1_hex_4, syscall_decoder_1_hex_3, syscall_decoder_1_hex_2, syscall_decoder_1_hex}));
  // alu alu_1: pin names not known; wires that end beside it: multiplexer_15_out
  Button button_2 (.out(ExpSrc1));
  Button button_3 (.out(ExpSrc2));
  RAM #(.addrWidth(10), .dataWidth(32)) ram_1 (
    .addr(undriven[11:2]), .we(MemWrite), .oe(MemRead), .clk(Clk), .din(immediate_extender_1_p3),
    .dout(ram_1_dout));
  Shifter #(.width(32)) shifter_1 (.in(immediate_extender_1_p3), .\dist ({5{1'b0}}), .out(shifter_1_out));
  xor xor_1 (xor_1_out, Equal, BneOrBeq);
  Hex_Digit_Display hex_digit_display_1 (.value(syscall_decoder_1_hex_5));  // open: dp
  Hex_Digit_Display hex_digit_display_2 (.value(syscall_decoder_1_hex_4));  // open: dp
  Adder #(.width(32)) adder_3 (
    .a({adder_1_out_2, adder_1_out}), .b(shifter_1_out), .out(adder_3_out));  // open: cin, cout
  Hex_Digit_Display hex_digit_display_3 (.value(syscall_decoder_1_hex_3));  // open: dp
  Hex_Digit_Display hex_digit_display_4 (.value(syscall_decoder_1_hex_2));  // open: dp
  and and_2 (and_2_out, Branch, xor_1_out);
  Hex_Digit_Display hex_digit_display_5 (.value(syscall_decoder_1_hex[15:12]));  // open: dp
  Hex_Digit_Display hex_digit_display_6 (.value(syscall_decoder_1_hex[11:8]));  // open: dp
  Multiplexer #(.width(32)) multiplexer_16 (
    .in0({adder_1_out_2, adder_1_out}), .in1(adder_3_out), .out(multiplexer_16_out), .sel(and_2_out));
  not not_5 (not_5_out, Jump);
  Hex_Digit_Display hex_digit_display_7 (.value(syscall_decoder_1_hex[7:4]));  // open: dp
  Hex_Digit_Display hex_digit_display_8 (.value(syscall_decoder_1_hex[3:0]));  // open: dp
  Multiplexer #(.width(32)) multiplexer_17 (.in0(undriven), .in1(ram_1_dout), .out(multiplexer_17_out), .sel(MemtoReg));
  Multiplexer #(.width(32)) multiplexer_18 (
    .in0({adder_1_out_2, multiplexer_5_out, 2'b00}), .in1(multiplexer_16_out), .out(multiplexer_18_out),
    .sel(not_5_out));
  Multiplexer #(.width(32)) multiplexer_19 (
    .in0(multiplexer_18_out), .in1(regfile_1_p4), .out(multiplexer_19_out), .sel(isJR));

  // Notes on the sheet:
  //   PC
  //   Cycles
  //   Total Cycles
  //   R
  //   J
  //   contents of rom_1 (hex, n*v repeats v):
  //   20110001 8000c05 20110001 20120002 20130003 8000c09 20110001 20120002 20130003 8000c0d 20110001
  //   20120002 20130003 8000c11 20110001 20120002 20130003 c000d2e 20100001 20110001 118fc0 112020
  //   20020022 c 118882 12200001 8000c15 112020 20020022 c 20110001 118880 112020 20020022 c 12200001
  //   8000c1f 20110001 118fc0 112020 20020022 c 1188c3 112020 20020022 c 118903 112020 20020022 c 118903
  //   112020 20020022 c 118903 112020 20020022 c 118903 112020 20020022 c 118903 112020 20020022 c 118903
  //   112020 20020022 c 118903 112020 20020022 c 20100001 109fc0 139fc3 8021 2012000c 24160003 26100001
  //   3210000f 20080008 20090001 139900 2709825 132020 20020022 c 1094022 1500fff9 22100001 2018000f
  //   2188024 108700 20080008 20090001 139902 2709825 132021 20020022 c 1094022 1500fff9 108702 2c9b022
  //   12c00001 8000c50 4020 1084027 84400 3508ffff 82021 20020022 c 20110004 ae310000 8e320000 2252fffc
  //   20100000 22110001 2118020 22520004 ae500000 22310001 2118020 22520004 ae500000 22310001 2118020
  //   22520004 ae500000 22310001 2118020 22520004 ae500000 22310001 2118020 22520004 ae500000 22310001
  //   2118020 22520004 ae500000 22310001 2118020 22520004 ae500000 20090001 8c080004 1509008f ac000004
  //   20090003 8c080008 1509008b ac000008 20090006 8c08000c 15090087 ac00000c 2009000a 8c080010 15090083
  //   ac000010 2009000f 8c080014 1509007f ac000014 20090015 8c080018 1509007b ac000018 2009001c 8c08001c
  //   15090077 ac00001c 2010ffff 20110000 ae300000 22100001 22310004 ae300000 22100001 22310004 ae300000
  //   22100001 22310004 ae300000 22100001 22310004 ae300000 22100001 22310004 ae300000 22100001 22310004
  //   ae300000 22100001 22310004 ae300000 22100001 22310004 ae300000 22100001 22310004 ae300000 22100001
  //   22310004 ae300000 22100001 22310004 ae300000 22100001 22310004 ae300000 22100001 22310004 ae300000
  //   22100001 22310004 ae300000 22100001 22310004 ae300000 22100001 22310004 22100001 8020 2011003c
  //   8e130000 8e340000 274402a 11000002 ae330000 ae140000 2231fffc 1611fff8 102020 20020022 c 22100004
  //   2011003c 1611fff2 20100001 201200ff 20110001 20130003 12120005 12100004 20110001 20120002 20130003
  //   8000d26 102020 20020001 c 16310005 16320004 20110001 20120002 20130003 8000d26 132020 20020001 c
  //   2011ffff 118c00 2020 24840064 2484ff9c 14800017 2020 2484ff9c 24840064 14800013 2020 34847fff 912024
  //   1480000f 2020 34848000 912024 1480000b 24040000 8000d20 8000d26 2002000a c 20041ced 42400 3484cafe
  //   20020022 c 8000d1e 3c010000 3421baad 12020 42400 3484c0de 20020022 c 8000d1e 20100000 22100001
  //   102020 20020022 c 22100002 102020 20020022 c 22100003 102020 20020022 c 22100004 102020 20020022 c
  //   22100005 102020 20020022 c 22100006 102020 20020022 c 22100007 102020 20020022 c 22100008 102020
  //   20020022 c 3e00008
  //   R
  //   PC Buffer
endmodule
